// Logisim project Domaci_rad_2.circ as structural Verilog: 1 circuit, main circuit Domaci2
module Domaci2 (
  input  x1,
  input  x2,
  input  x3,
  input  x4,
  input  x5,
  output out_6
);

  wire nor_1_out, nor_2_out, nor_3_out, nor_4_out, nor_5_out, nor_6_out, nor_7_out;

  nor nor_1 (nor_1_out, x1, x2);
  nor nor_2 (nor_2_out, nor_1_out, nor_1_out);
  nor nor_3 (nor_3_out, x3, x3);
  nor nor_4 (nor_4_out, nor_2_out, nor_3_out);
  nor nor_5 (nor_5_out, x4, x5);
  nor nor_6 (nor_6_out, nor_4_out, nor_4_out);
  nor nor_7 (nor_7_out, nor_5_out, nor_5_out);
  nor nor_8 (out_6, nor_6_out, nor_7_out);
endmodule
