// Logisim project Vezba.circ as structural Verilog: 1 circuit, main circuit Vezba
module Vezba (
  input  x1,
  input  x2,
  output y
);

  wire not_1_out, not_2_out, or_1_out, or_2_out;

  // Probe on not_1_out
  not not_1 (not_1_out, x2);
  not not_2 (not_2_out, x1);
  // Probe on not_2_out
  or or_1 (or_1_out, x1, not_1_out);
  or or_2 (or_2_out, not_2_out, x2);
  // Probe on or_1_out
  // Probe on or_2_out
  and and_1 (y, or_1_out, or_2_out);
endmodule
